// Logisim project Lab01.circ as structural Verilog: 5 circuits, main circuit led计数
module \led计数  (
  input  in1,
  input  in2,
  input  in3,
  input  in4,
  input  in5,
  output out1,
  output out2,
  output out3,
  output out4,
  output out5
);

  or or_1 (out1, in1, in2, in3, in4, in5);
  or or_2 (out2, in2, in3, in4, in5);
  or or_3 (out3, in3, in4, in5);
  or or_4 (out4, in4, in5);

  assign out5 = in5;
endmodule

module \led测试  (
);

  wire _1_out, _2_out, _3_out, _4_out, _5_out, \led计数_1_out1 , \led计数_1_out2 , \led计数_1_out3 ,
       \led计数_1_out4 , \led计数_1_out5 , \n7段数码管表示_1_out1 , \n7段数码管表示_1_out2 , \n7段数码管表示_1_out3 ,
       \n7段数码管表示_1_out4 , \n7段数码管表示_1_out5 , \n7段数码管表示_1_out6 , \n7段数码管表示_1_out7 ;
  wire [2:0] \按键编码_1_low ;

  Button _1 (.out(_1_out));
  Button _2 (.out(_2_out));
  Button _3 (.out(_3_out));
  Button _4 (.out(_4_out));
  Button _5 (.out(_5_out));
  \led计数  \led计数_1  (
    .out1(\led计数_1_out1 ), .in1(_1_out), .in2(_2_out), .in3(_3_out), .in4(_4_out), .in5(_5_out),
    .out2(\led计数_1_out2 ), .out3(\led计数_1_out3 ), .out4(\led计数_1_out4 ), .out5(\led计数_1_out5 ));
  \按键编码  \u_按键编码_1  (
    .in1(_1_out), .in2(_2_out), .in3(_3_out), .in4(_4_out), .in5(_5_out), .low(\按键编码_1_low [0]),
    .mid(\按键编码_1_low [1]), .high(\按键编码_1_low [2]));
  LED led_1 (.in(\led计数_1_out1 ));
  LED led_2 (.in(\led计数_1_out2 ));
  LED led_3 (.in(\led计数_1_out3 ));
  LED led_4 (.in(\led计数_1_out4 ));
  LED led_5 (.in(\led计数_1_out5 ));
  // Probe on {1'b0, \按键编码_1_low }
  Hex_Digit_Display hex_digit_display_1 (.value({1'b0, \按键编码_1_low }), .dp(1'b1));
  \_7段数码管表示  \u_7段数码管表示_1  (
    .in1(\按键编码_1_low [0]), .in2(\按键编码_1_low [1]), .in3(\按键编码_1_low [2]), .out1(\n7段数码管表示_1_out1 ),
    .in4(1'b0), .out2(\n7段数码管表示_1_out2 ), .out3(\n7段数码管表示_1_out3 ), .out4(\n7段数码管表示_1_out4 ),
    .out5(\n7段数码管表示_1_out5 ), .out6(\n7段数码管表示_1_out6 ), .out7(\n7段数码管表示_1_out7 ));
  _7_Segment_Display u_7_segment_display_1 (
    .g(\n7段数码管表示_1_out1 ), .f(\n7段数码管表示_1_out2 ), .a(\n7段数码管表示_1_out3 ), .b(\n7段数码管表示_1_out4 ),
    .e(\n7段数码管表示_1_out5 ), .d(\n7段数码管表示_1_out6 ), .c(\n7段数码管表示_1_out7 ), .dp(1'b1));
endmodule

module \按键编码  (
  input  in1,
  input  in2,
  input  in3,
  input  in4,
  input  in5,
  output low,
  output mid,
  output high
);

  wire and_1_out, and_2_out, and_3_out, and_4_out, and_5_out, and_6_out, and_7_out, and_8_out, and_9_out,
       not_1_out, not_2_out, not_3_out, not_4_out, not_5_out, not_6_out, not_7_out, not_8_out, not_9_out,
       not_10_out, not_11_out, not_12_out, not_13_out, not_14_out;

  not not_1 (not_1_out, in1);
  not not_2 (not_2_out, in4);
  not not_3 (not_3_out, in4);
  not not_4 (not_4_out, in2);
  not not_5 (not_5_out, in3);
  not not_6 (not_6_out, in4);
  not not_7 (not_7_out, in4);
  not not_8 (not_8_out, in5);
  not not_9 (not_9_out, in4);
  not not_10 (not_10_out, in5);
  not not_11 (not_11_out, in2);
  not not_12 (not_12_out, in5);
  not not_13 (not_13_out, in1);
  not not_14 (not_14_out, in3);
  and and_1 (and_1_out, not_1_out, in3, not_2_out);
  and and_2 (and_2_out, in2, in3, not_3_out);
  and and_3 (and_3_out, in1, not_4_out, not_5_out, not_6_out);
  and and_4 (and_4_out, in3, not_7_out, not_8_out);
  and and_5 (and_5_out, in2, not_9_out, not_10_out);
  and and_6 (and_6_out, in1, not_11_out, in3, not_12_out);
  and and_7 (and_7_out, not_13_out, in4);
  and and_8 (and_8_out, not_14_out, in4);
  and and_9 (and_9_out, in2, in4);
  or or_1 (low, in5, and_1_out, and_2_out, and_3_out);
  or or_2 (mid, and_4_out, and_5_out, and_6_out);
  or or_3 (high, in5, and_7_out, and_8_out, and_9_out);
endmodule

module \_7段数码管表示  (
  input  in1,
  input  in2,
  input  in3,
  input  in4,
  output out1,
  output out2,
  output out3,
  output out4,
  output out5,
  output out6,
  output out7
);

  wire and_1_out, and_2_out, and_3_out, and_4_out, and_5_out, and_6_out, and_7_out, and_8_out, and_9_out,
       and_10_out, and_11_out, and_12_out, and_13_out, and_14_out, and_15_out, and_16_out, and_17_out,
       and_18_out, and_19_out, and_20_out, and_21_out, and_22_out, and_23_out, and_24_out, and_25_out,
       and_26_out, and_27_out, and_28_out, and_29_out, and_30_out, and_31_out, and_32_out, and_33_out,
       and_34_out, and_35_out, not_1_out, not_2_out, not_3_out, not_4_out, not_5_out, not_6_out, not_7_out,
       not_8_out, not_9_out, not_10_out, not_11_out, not_12_out, not_13_out, not_14_out, not_15_out,
       not_16_out, not_17_out, not_18_out, not_19_out, not_20_out, not_21_out, not_22_out, not_23_out,
       not_24_out, not_25_out, not_26_out, not_27_out, not_28_out, not_29_out, not_30_out, not_31_out,
       not_32_out, not_33_out, not_34_out, not_35_out, not_36_out, not_37_out, not_38_out, not_39_out,
       not_40_out, not_41_out, not_42_out, not_43_out, not_44_out;

  not not_1 (not_1_out, in3);
  and and_1 (and_1_out, not_1_out, in4);
  not not_2 (not_2_out, in2);
  and and_2 (and_2_out, not_2_out, in3, not_3_out);
  not not_3 (not_3_out, in4);
  not not_4 (not_4_out, in1);
  and and_3 (and_3_out, not_4_out, in2);
  and and_4 (and_4_out, in2, not_5_out);
  not not_5 (not_5_out, in3);
  and and_5 (and_5_out, in1, in4);
  not not_6 (not_6_out, in1);
  and and_6 (and_6_out, not_6_out, not_7_out);
  not not_7 (not_7_out, in2);
  not not_8 (not_8_out, in3);
  and and_7 (and_7_out, not_8_out, in4);
  not not_9 (not_9_out, in1);
  and and_8 (and_8_out, not_9_out, in3);
  not not_10 (not_10_out, in2);
  and and_9 (and_9_out, not_10_out, in3, not_11_out);
  not not_11 (not_11_out, in4);
  and and_10 (and_10_out, in2, in4);
  not not_12 (not_12_out, in1);
  and and_11 (and_11_out, not_12_out, not_13_out);
  not not_13 (not_13_out, in3);
  not not_14 (not_14_out, in1);
  and and_12 (and_12_out, not_14_out, in4);
  not not_15 (not_15_out, in2);
  not not_16 (not_16_out, in3);
  and and_13 (and_13_out, not_15_out, not_16_out, in4);
  and and_14 (and_14_out, in2, not_17_out);
  not not_17 (not_17_out, in4);
  and and_15 (and_15_out, in2, in3);
  and and_16 (and_16_out, in1, in3, not_18_out);
  not not_18 (not_18_out, in4);
  not not_19 (not_19_out, in1);
  and and_17 (and_17_out, not_19_out, not_20_out, not_21_out);
  not not_20 (not_20_out, in2);
  not not_21 (not_21_out, in4);
  not not_22 (not_22_out, in1);
  and and_18 (and_18_out, not_22_out, not_23_out);
  not not_23 (not_23_out, in3);
  not not_24 (not_24_out, in2);
  and and_19 (and_19_out, not_24_out, not_25_out);
  not not_25 (not_25_out, in3);
  and and_20 (and_20_out, in1, not_26_out, in4);
  not not_26 (not_26_out, in2);
  and and_21 (and_21_out, in1, in2, not_27_out);
  not not_27 (not_27_out, in4);
  not not_28 (not_28_out, in1);
  and and_22 (and_22_out, not_28_out, not_29_out);
  not not_29 (not_29_out, in3);
  and and_23 (and_23_out, in3, in4);
  not not_30 (not_30_out, in1);
  and and_24 (and_24_out, not_30_out, in2);
  and and_25 (and_25_out, in2, in4);
  not not_31 (not_31_out, in1);
  and and_26 (and_26_out, not_31_out, not_32_out, not_33_out);
  not not_32 (not_32_out, in2);
  not not_33 (not_33_out, in3);
  not not_34 (not_34_out, in1);
  and and_27 (and_27_out, not_34_out, in3, in4);
  not not_35 (not_35_out, in1);
  and and_28 (and_28_out, not_35_out, in2, not_36_out);
  not not_36 (not_36_out, in4);
  and and_29 (and_29_out, in1, not_37_out, in3);
  not not_37 (not_37_out, in2);
  and and_30 (and_30_out, in1, in2, not_38_out);
  not not_38 (not_38_out, in3);
  not not_39 (not_39_out, in2);
  and and_31 (and_31_out, not_39_out, not_40_out);
  not not_40 (not_40_out, in3);
  not not_41 (not_41_out, in3);
  and and_32 (and_32_out, not_41_out, in4);
  and and_33 (and_33_out, in3, not_42_out);
  not not_42 (not_42_out, in4);
  and and_34 (and_34_out, in1, not_43_out);
  not not_43 (not_43_out, in2);
  and and_35 (and_35_out, in1, not_44_out);
  not not_44 (not_44_out, in3);
  or or_1 (out1, and_1_out, and_2_out, and_3_out, and_4_out, and_5_out);
  or or_2 (out2, and_6_out, and_7_out, and_8_out, and_9_out, and_10_out);
  or or_3 (out4, and_17_out, and_18_out, and_19_out, and_20_out, and_21_out);
  or or_4 (out5, and_22_out, and_23_out, and_24_out, and_25_out);
  or or_5 (out6, and_26_out, and_27_out, and_28_out, and_29_out, and_30_out);
  or or_6 (out7, and_31_out, and_32_out, and_33_out, and_34_out, and_35_out);
  or or_7 (out3, and_11_out, and_12_out, and_13_out, and_14_out, and_15_out, and_16_out);
endmodule

module \数码管驱动自动测试  (
);

  wire clock_1_out, \n7段数码管表示_1_out1 , \n7段数码管表示_1_out2 , \n7段数码管表示_1_out3 , \n7段数码管表示_1_out4 ,
       \n7段数码管表示_1_out5 , \n7段数码管表示_1_out6 , \n7段数码管表示_1_out7 ;
  wire [3:0] counter_1_q;

  Counter #(.width(4), .max('hf)) counter_1 (
    .Q(counter_1_q), .clk(clock_1_out));  // open: load, D, count, carry, clr, preset, down
  Clock clock_1 (.out(clock_1_out));
  \_7段数码管表示  \u_7段数码管表示_1  (
    .in1(counter_1_q[0]), .in2(counter_1_q[1]), .in3(counter_1_q[2]), .out1(\n7段数码管表示_1_out1 ),
    .in4(counter_1_q[3]), .out2(\n7段数码管表示_1_out2 ), .out3(\n7段数码管表示_1_out3 ), .out4(\n7段数码管表示_1_out4 ),
    .out5(\n7段数码管表示_1_out5 ), .out6(\n7段数码管表示_1_out6 ), .out7(\n7段数码管表示_1_out7 ));
  _7_Segment_Display u_7_segment_display_1 (
    .g(\n7段数码管表示_1_out1 ), .f(\n7段数码管表示_1_out2 ), .a(\n7段数码管表示_1_out3 ), .b(\n7段数码管表示_1_out4 ),
    .e(\n7段数码管表示_1_out5 ), .d(\n7段数码管表示_1_out6 ), .c(\n7段数码管表示_1_out7 ));  // open: dp
endmodule
