// Logisim project Lab02.circ as structural Verilog: 5 circuits, main circuit 一位二路选择器
module \一位二路选择器  (
  input  x,
  input  sel,
  input  y,
  output out
);

  wire and_1_out, and_2_out, not_1_out;

  not not_1 (not_1_out, sel);
  and and_1 (and_1_out, x, not_1_out);
  and and_2 (and_2_out, sel, y);
  or or_1 (out, and_1_out, and_2_out);
endmodule

module \十六位二路选择器  (
  input  [15:0] x,
  input  [15:0] y,
  input  sel,
  output [15:0] out
);

  \一位二路选择器  \u_一位二路选择器_1  (.x(x[0]), .sel(sel), .y(y[0]), .out(out[0]));
  \一位二路选择器  \u_一位二路选择器_2  (.x(x[1]), .sel(sel), .y(y[1]), .out(out[1]));
  \一位二路选择器  \u_一位二路选择器_3  (.x(x[2]), .sel(sel), .y(y[2]), .out(out[2]));
  \一位二路选择器  \u_一位二路选择器_4  (.x(x[3]), .sel(sel), .y(y[3]), .out(out[3]));
  \一位二路选择器  \u_一位二路选择器_5  (.x(x[4]), .sel(sel), .y(y[4]), .out(out[4]));
  \一位二路选择器  \u_一位二路选择器_6  (.x(x[5]), .sel(sel), .y(y[5]), .out(out[5]));
  \一位二路选择器  \u_一位二路选择器_7  (.x(x[6]), .sel(sel), .y(y[6]), .out(out[6]));
  \一位二路选择器  \u_一位二路选择器_8  (.x(x[7]), .sel(sel), .y(y[7]), .out(out[7]));
  \一位二路选择器  \u_一位二路选择器_9  (.x(x[8]), .sel(sel), .y(y[8]), .out(out[8]));
  \一位二路选择器  \u_一位二路选择器_10  (.x(x[9]), .sel(sel), .y(y[9]), .out(out[9]));
  \一位二路选择器  \u_一位二路选择器_11  (.x(x[10]), .sel(sel), .y(y[10]), .out(out[10]));
  \一位二路选择器  \u_一位二路选择器_12  (.x(x[11]), .sel(sel), .y(y[11]), .out(out[11]));
  \一位二路选择器  \u_一位二路选择器_13  (.x(x[12]), .sel(sel), .y(y[12]), .out(out[12]));
  \一位二路选择器  \u_一位二路选择器_14  (.x(x[13]), .sel(sel), .y(y[13]), .out(out[13]));
  \一位二路选择器  \u_一位二路选择器_15  (.x(x[14]), .sel(sel), .y(y[14]), .out(out[14]));
  \一位二路选择器  \u_一位二路选择器_16  (.x(x[15]), .sel(sel), .y(y[15]), .out(out[15]));
endmodule

module \_2位无符号比较器  (
  input  a1,
  input  a0,
  input  b1,
  input  b0,
  output out_5,
  output out_6,
  output out_7
);

  wire and_1_out, and_2_out, and_3_out, and_4_out, and_5_out, and_6_out, and_7_out, and_8_out, and_9_out,
       and_10_out, not_1_out, not_2_out, not_3_out, not_4_out, not_5_out, not_6_out, not_7_out, not_8_out,
       not_9_out, not_10_out, not_11_out, not_12_out, not_13_out, not_14_out, not_15_out, not_16_out;

  not not_1 (not_1_out, b1);
  and and_1 (and_1_out, a0, not_1_out, not_2_out);
  not not_2 (not_2_out, b0);
  and and_2 (and_2_out, a1, not_3_out);
  not not_3 (not_3_out, b1);
  and and_3 (and_3_out, a1, a0, not_4_out);
  not not_4 (not_4_out, b0);
  not not_5 (not_5_out, a1);
  not not_6 (not_6_out, a0);
  not not_7 (not_7_out, b1);
  not not_8 (not_8_out, b0);
  not not_9 (not_9_out, a1);
  not not_10 (not_10_out, b1);
  not not_11 (not_11_out, a0);
  not not_12 (not_12_out, b0);
  not not_13 (not_13_out, a1);
  and and_4 (and_4_out, not_13_out, not_14_out, b0);
  not not_14 (not_14_out, a0);
  not not_15 (not_15_out, a1);
  and and_5 (and_5_out, not_15_out, b1);
  not not_16 (not_16_out, a0);
  and and_6 (and_6_out, not_16_out, b1, b0);
  or or_1 (out_5, and_1_out, and_2_out, and_3_out);
  and and_7 (and_7_out, not_5_out, not_6_out, not_7_out, not_8_out);
  and and_8 (and_8_out, not_9_out, a0, not_10_out, b0);
  and and_9 (and_9_out, a1, not_11_out, b1, not_12_out);
  and and_10 (and_10_out, a1, a0, b1, b0);
  or or_2 (out_7, and_4_out, and_5_out, and_6_out);
  or or_3 (out_6, and_7_out, and_8_out, and_9_out, and_10_out);
endmodule

module \_4位无符号比较器  (
  input  [3:0] a,
  input  [3:0] b,
  output out_3,
  output out_4,
  output out_5
);

  wire and_1_out, and_2_out, \n2位无符号比较器_1_out_5 , \n2位无符号比较器_1_out_6 , \n2位无符号比较器_1_out_7 ,
       \n2位无符号比较器_2_out_5 , \n2位无符号比较器_2_out_6 , \n2位无符号比较器_2_out_7 ;

  \_2位无符号比较器  \u_2位无符号比较器_1  (
    .a1(a[1]), .a0(a[0]), .b1(b[1]), .b0(b[0]), .out_5(\n2位无符号比较器_1_out_5 ), .out_6(\n2位无符号比较器_1_out_6 ),
    .out_7(\n2位无符号比较器_1_out_7 ));
  \_2位无符号比较器  \u_2位无符号比较器_2  (
    .a1(a[3]), .a0(a[2]), .b1(b[3]), .b0(b[2]), .out_5(\n2位无符号比较器_2_out_5 ), .out_6(\n2位无符号比较器_2_out_6 ),
    .out_7(\n2位无符号比较器_2_out_7 ));
  and and_1 (and_1_out, \n2位无符号比较器_2_out_6 , \n2位无符号比较器_1_out_5 );
  and and_2 (and_2_out, \n2位无符号比较器_1_out_7 , \n2位无符号比较器_2_out_6 );
  or or_1 (out_3, and_1_out, \n2位无符号比较器_2_out_5 );
  and and_3 (out_4, \n2位无符号比较器_1_out_6 , \n2位无符号比较器_2_out_6 );
  or or_2 (out_5, and_2_out, \n2位无符号比较器_2_out_7 );
endmodule

module \_16位无符号比较器  (
  input  [15:0] in_1,
  input  [15:0] in_2,
  output out_3,
  output out_4,
  output out_5
);

  wire and_1_out, and_2_out, and_3_out, and_4_out, and_5_out, and_6_out, \n4位无符号比较器_1_out_3 ,
       \n4位无符号比较器_1_out_4 , \n4位无符号比较器_1_out_5 , \n4位无符号比较器_2_out_3 , \n4位无符号比较器_2_out_4 ,
       \n4位无符号比较器_2_out_5 , \n4位无符号比较器_3_out_3 , \n4位无符号比较器_3_out_4 , \n4位无符号比较器_3_out_5 ,
       \n4位无符号比较器_4_out_3 , \n4位无符号比较器_4_out_4 , \n4位无符号比较器_4_out_5 ;

  \_4位无符号比较器  \u_4位无符号比较器_1  (
    .a(in_1[3:0]), .b(in_2[3:0]), .out_3(\n4位无符号比较器_1_out_3 ), .out_4(\n4位无符号比较器_1_out_4 ),
    .out_5(\n4位无符号比较器_1_out_5 ));
  \_4位无符号比较器  \u_4位无符号比较器_2  (
    .a(in_1[7:4]), .b(in_2[7:4]), .out_3(\n4位无符号比较器_2_out_3 ), .out_4(\n4位无符号比较器_2_out_4 ),
    .out_5(\n4位无符号比较器_2_out_5 ));
  \_4位无符号比较器  \u_4位无符号比较器_3  (
    .a(in_1[11:8]), .b(in_2[11:8]), .out_3(\n4位无符号比较器_3_out_3 ), .out_4(\n4位无符号比较器_3_out_4 ),
    .out_5(\n4位无符号比较器_3_out_5 ));
  \_4位无符号比较器  \u_4位无符号比较器_4  (
    .a(in_1[15:12]), .b(in_2[15:12]), .out_3(\n4位无符号比较器_4_out_3 ), .out_4(\n4位无符号比较器_4_out_4 ),
    .out_5(\n4位无符号比较器_4_out_5 ));
  and and_1 (and_1_out, \n4位无符号比较器_2_out_5 , \n4位无符号比较器_3_out_4 , \n4位无符号比较器_4_out_4 );
  and and_2 (and_2_out, \n4位无符号比较器_3_out_5 , \n4位无符号比较器_4_out_4 );
  and and_3 (and_3_out, \n4位无符号比较器_1_out_5 , \n4位无符号比较器_2_out_4 , \n4位无符号比较器_3_out_4 , \n4位无符号比较器_4_out_4 );
  and and_4 (and_4_out, \n4位无符号比较器_2_out_3 , \n4位无符号比较器_3_out_4 , \n4位无符号比较器_4_out_4 );
  and and_5 (and_5_out, \n4位无符号比较器_3_out_3 , \n4位无符号比较器_4_out_4 );
  and and_6 (and_6_out, \n4位无符号比较器_1_out_3 , \n4位无符号比较器_2_out_4 , \n4位无符号比较器_3_out_4 , \n4位无符号比较器_4_out_4 );
  or or_1 (out_3, and_6_out, and_4_out, and_5_out, \n4位无符号比较器_4_out_3 );
  and and_7 (out_4, \n4位无符号比较器_1_out_4 , \n4位无符号比较器_2_out_4 , \n4位无符号比较器_3_out_4 , \n4位无符号比较器_4_out_4 );
  or or_2 (out_5, and_3_out, and_1_out, and_2_out, \n4位无符号比较器_4_out_5 );
endmodule
